// Logisim project bitpacker.circ as structural Verilog: 1 circuit, main circuit main
module main (
  input  [15:0] in_1,
  input  [4:0] in_2,
  output [15:0] out_3,
  output out_4
);

  wire clock_1_out, clock_2_out, clock_3_out;
  wire [3:0] adder_2_out, register_1_q;
  wire [4:0] bit_extender_2_out;
  wire [4:4] adder_2_out_2;
  wire [15:0] multiplexer_1_out, or_1_out, register_2_q;
  wire [31:0] adder_1_out, and_1_out, bit_extender_1_out, shifter_1_out, shifter_2_out;

  Shifter #(.width(32)) shifter_1 (.in(32'h1), .\dist (in_2), .out(shifter_1_out));
  Clock clock_1 (.out(clock_1_out));
  assign bit_extender_1_out = {{16{1'b0}}, in_1};  // Bit_Extender bit_extender_1
  Adder #(.width(32)) adder_1 (.a(shifter_1_out), .b({32{1'b1}}), .out(adder_1_out));  // open: cin, cout
  Register #(.width(4)) register_1 (.D(adder_2_out), .Q(register_1_q), .clk(clock_1_out));  // open: en, clr
  assign and_1_out = bit_extender_1_out & adder_1_out;  // AND_Gate and_1, 32 bits wide
  assign bit_extender_2_out = {{1{1'b0}}, register_1_q};  // Bit_Extender bit_extender_2
  Shifter #(.width(32)) shifter_2 (.in(and_1_out), .\dist (bit_extender_2_out), .out(shifter_2_out));
  Adder #(.width(5)) adder_2 (
    .a(in_2), .b(bit_extender_2_out), .out({adder_2_out_2[4], adder_2_out}), .cin(1'b0));  // open: cout
  Multiplexer #(.width(16), .disabled(0), .enable("false")) multiplexer_1 (
    .in0(or_1_out), .in1(shifter_2_out[31:16]), .out(multiplexer_1_out), .sel(adder_2_out_2[4]));
  Clock clock_2 (.out(clock_2_out));
  Register #(.width(16)) register_2 (.D(multiplexer_1_out), .Q(register_2_q), .clk(clock_2_out));  // open: en, clr
  assign or_1_out = register_2_q | shifter_2_out[15:0];  // OR_Gate or_1, 16 bits wide
  Clock clock_3 (.out(clock_3_out));
  Register #(.width(16)) register_3 (.D(or_1_out), .Q(out_3), .clk(clock_3_out));  // open: en, clr
  D_Flip_Flop d_ff_1 (.clk(clock_3_out), .D(adder_2_out_2[4]), .Q(out_4));  // open: Qn, preset, en, reset
endmodule
