// Logisim project loeffler_dct_8.circ as structural Verilog: 2 circuits, main circuit main
module main (
  input  [2:0] in_1,
  output [7:0] out_2
);

  wire clock_1_out, clock_2_out, clock_3_out, clock_4_out, clock_5_out, decoder_1_out0, decoder_1_out1,
       not_1_out;
  wire [2:0] register_2_q;
  wire [7:0] counter_1_q, register_3_q, rom_2_data, rom_3_data;
  wire [14:0] rom_1_data;
  wire [15:0] adder_1_out, bit_extender_1_out, dual_port_ram_1_rdata, multiplexer_1_out, multiplexer_2_out,
       negator_1_out, register_4_q, register_5_q;

  Counter counter_1 (.Q(counter_1_q), .clk(clock_1_out));  // open: load, D, count, carry, clr
  Clock clock_1 (.out(clock_1_out));
  Clock clock_2 (.out(clock_2_out));
  ROM #(.dataWidth(15)) rom_1 (.addr(counter_1_q), .data(rom_1_data));  // open: sel
  Clock clock_3 (.out(clock_3_out));
  ROM #(.addrWidth(3)) rom_2 (.addr(in_1), .data(rom_2_data));  // open: sel
  Register register_1 (.D(rom_2_data), .Q(out_2), .clk(clock_2_out));  // open: en, clr
  Register #(.width(3)) register_2 (.D(rom_1_data[2:0]), .Q(register_2_q), .clk(clock_3_out));  // open: en, clr
  Clock clock_4 (.out(clock_4_out));
  dual_port_ram dual_port_ram_1 (
    .WCLK(clock_4_out), .WDATA(adder_1_out), .WE(rom_1_data[7]), .WADDR(rom_1_data[12:8]),
    .RDATA(dual_port_ram_1_rdata), .RADDR(rom_1_data[4:0]), .RCLK(clock_4_out));
  Register register_3 (.D(rom_3_data), .Q(register_3_q), .clk(not_1_out));  // open: en, clr
  ROM #(.addrWidth(3)) rom_3 (.addr(register_2_q), .data(rom_3_data));  // open: sel
  not not_1 (not_1_out, clock_3_out);
  assign bit_extender_1_out = {{8{register_3_q[7]}}, register_3_q};  // Bit_Extender bit_extender_1
  Multiplexer #(.width(16), .disabled(0), .enable("false")) multiplexer_1 (
    .in0(bit_extender_1_out), .in1(dual_port_ram_1_rdata), .out(multiplexer_1_out), .sel(rom_1_data[13]));
  Multiplexer #(.width(16), .disabled(0), .enable("false")) multiplexer_2 (
    .in0(multiplexer_1_out), .in1(negator_1_out), .out(multiplexer_2_out), .sel(rom_1_data[14]));
  Negator #(.width(16)) negator_1 (.in(multiplexer_1_out), .out(negator_1_out));
  Decoder #(.disabled(0)) decoder_1 (
    .out0(decoder_1_out0), .out1(decoder_1_out1), .sel(rom_1_data[6]), .en(rom_1_data[5]));
  Register #(.width(16)) register_4 (
    .D(multiplexer_2_out), .en(decoder_1_out0), .Q(register_4_q), .clk(clock_5_out));  // open: clr
  Register #(.width(16)) register_5 (
    .D(multiplexer_2_out), .en(decoder_1_out1), .Q(register_5_q), .clk(clock_5_out));  // open: clr
  Clock clock_5 (.out(clock_5_out));
  Adder #(.width(16)) adder_1 (.a(register_4_q), .b(register_5_q), .out(adder_1_out), .cin(1'b0));  // open: cout

  // Notes on the sheet:
  //   contents of rom_1 (hex, n*v repeats v):
  //   0 7 20 60 80 1 6 20 60 180
  //   contents of rom_2 (hex, n*v repeats v):
  //   1 2 3 4 5 6 7 8
  //   FFs on input and output are to mimic iCE40 sysMEM read timings
  //   8 Byte input memory buffer
  //   64 Byte internal scratchpad
  //   contents of rom_3 (hex, n*v repeats v):
  //   1 2 3 4 5 6 7 8
endmodule

module dual_port_ram (
  input  WCLK,
  input  [15:0] WDATA,
  input  RCLK,
  input  [4:0] RADDR,
  input  WE,
  input  [4:0] WADDR,
  output [15:0] RDATA
);

  wire decoder_1_out0, decoder_1_out1, decoder_1_out2, decoder_1_out3, decoder_1_out4, decoder_1_out5,
       decoder_1_out6, decoder_1_out7, decoder_1_out8, decoder_1_out9, decoder_1_out10, decoder_1_out11,
       decoder_1_out12, decoder_1_out13, decoder_1_out14, decoder_1_out15, decoder_1_out16, decoder_1_out17,
       decoder_1_out18, decoder_1_out19, decoder_1_out20, decoder_1_out21, decoder_1_out22, decoder_1_out23,
       decoder_1_out24, decoder_1_out25, decoder_1_out26, decoder_1_out27, decoder_1_out28, decoder_1_out29,
       decoder_1_out30, decoder_1_out31, not_1_out;
  wire [15:0] multiplexer_1_out, register_1_q, register_2_q, register_3_q, register_4_q, register_5_q,
       register_6_q, register_7_q, register_8_q, register_9_q, register_10_q, register_11_q, register_12_q,
       register_13_q, register_14_q, register_15_q, register_16_q, register_17_q, register_18_q,
       register_19_q, register_20_q, register_21_q, register_22_q, register_23_q, register_24_q,
       register_25_q, register_26_q, register_27_q, register_28_q, register_29_q, register_30_q,
       register_31_q, register_32_q, register_34_q;

  Decoder #(.select(5), .disabled(0)) decoder_1 (
    .out0(decoder_1_out0), .out1(decoder_1_out1), .out2(decoder_1_out2), .out3(decoder_1_out3),
    .out4(decoder_1_out4), .out5(decoder_1_out5), .out6(decoder_1_out6), .out7(decoder_1_out7),
    .out8(decoder_1_out8), .out9(decoder_1_out9), .out10(decoder_1_out10), .out11(decoder_1_out11),
    .out12(decoder_1_out12), .out13(decoder_1_out13), .out14(decoder_1_out14), .out15(decoder_1_out15),
    .out16(decoder_1_out16), .out17(decoder_1_out17), .out18(decoder_1_out18), .out19(decoder_1_out19),
    .out20(decoder_1_out20), .out21(decoder_1_out21), .out22(decoder_1_out22), .out23(decoder_1_out23),
    .out24(decoder_1_out24), .out25(decoder_1_out25), .out26(decoder_1_out26), .out27(decoder_1_out27),
    .out28(decoder_1_out28), .out29(decoder_1_out29), .out30(decoder_1_out30), .out31(decoder_1_out31),
    .sel(WADDR), .en(WE));
  Register #(.width(16)) register_1 (.D(WDATA), .en(decoder_1_out0), .Q(register_1_q), .clk(WCLK));  // open: clr
  Register #(.width(16)) register_2 (.D(WDATA), .en(decoder_1_out1), .Q(register_2_q), .clk(WCLK));  // open: clr
  Register #(.width(16)) register_3 (.D(WDATA), .en(decoder_1_out2), .Q(register_3_q), .clk(WCLK));  // open: clr
  Register #(.width(16)) register_4 (.D(WDATA), .en(decoder_1_out3), .Q(register_4_q), .clk(WCLK));  // open: clr
  Register #(.width(16)) register_5 (.D(WDATA), .en(decoder_1_out4), .Q(register_5_q), .clk(WCLK));  // open: clr
  Register #(.width(16)) register_6 (.D(WDATA), .en(decoder_1_out5), .Q(register_6_q), .clk(WCLK));  // open: clr
  Register #(.width(16)) register_7 (.D(WDATA), .en(decoder_1_out6), .Q(register_7_q), .clk(WCLK));  // open: clr
  Register #(.width(16)) register_8 (.D(WDATA), .en(decoder_1_out7), .Q(register_8_q), .clk(WCLK));  // open: clr
  Register #(.width(16)) register_9 (.D(WDATA), .en(decoder_1_out8), .Q(register_9_q), .clk(WCLK));  // open: clr
  Register #(.width(16)) register_10 (.D(WDATA), .en(decoder_1_out9), .Q(register_10_q), .clk(WCLK));  // open: clr
  Register #(.width(16)) register_11 (.D(WDATA), .en(decoder_1_out10), .Q(register_11_q), .clk(WCLK));  // open: clr
  Register #(.width(16)) register_12 (.D(WDATA), .en(decoder_1_out11), .Q(register_12_q), .clk(WCLK));  // open: clr
  Register #(.width(16)) register_13 (.D(WDATA), .en(decoder_1_out12), .Q(register_13_q), .clk(WCLK));  // open: clr
  Register #(.width(16)) register_14 (.D(WDATA), .en(decoder_1_out13), .Q(register_14_q), .clk(WCLK));  // open: clr
  Register #(.width(16)) register_15 (.D(WDATA), .en(decoder_1_out14), .Q(register_15_q), .clk(WCLK));  // open: clr
  Register #(.width(16)) register_16 (.D(WDATA), .en(decoder_1_out15), .Q(register_16_q), .clk(WCLK));  // open: clr
  Register #(.width(16)) register_17 (.D(WDATA), .en(decoder_1_out16), .Q(register_17_q), .clk(WCLK));  // open: clr
  Register #(.width(16)) register_18 (.D(WDATA), .en(decoder_1_out17), .Q(register_18_q), .clk(WCLK));  // open: clr
  Register #(.width(16)) register_19 (.D(WDATA), .en(decoder_1_out18), .Q(register_19_q), .clk(WCLK));  // open: clr
  Register #(.width(16)) register_20 (.D(WDATA), .en(decoder_1_out19), .Q(register_20_q), .clk(WCLK));  // open: clr
  Register #(.width(16)) register_21 (.D(WDATA), .en(decoder_1_out20), .Q(register_21_q), .clk(WCLK));  // open: clr
  Register #(.width(16)) register_22 (.D(WDATA), .en(decoder_1_out21), .Q(register_22_q), .clk(WCLK));  // open: clr
  Register #(.width(16)) register_23 (.D(WDATA), .en(decoder_1_out22), .Q(register_23_q), .clk(WCLK));  // open: clr
  Register #(.width(16)) register_24 (.D(WDATA), .en(decoder_1_out23), .Q(register_24_q), .clk(WCLK));  // open: clr
  Register #(.width(16)) register_25 (.D(WDATA), .en(decoder_1_out24), .Q(register_25_q), .clk(WCLK));  // open: clr
  Register #(.width(16)) register_26 (.D(WDATA), .en(decoder_1_out25), .Q(register_26_q), .clk(WCLK));  // open: clr
  Register #(.width(16)) register_27 (.D(WDATA), .en(decoder_1_out26), .Q(register_27_q), .clk(WCLK));  // open: clr
  Register #(.width(16)) register_28 (.D(WDATA), .en(decoder_1_out27), .Q(register_28_q), .clk(WCLK));  // open: clr
  Register #(.width(16)) register_29 (.D(WDATA), .en(decoder_1_out28), .Q(register_29_q), .clk(WCLK));  // open: clr
  Register #(.width(16)) register_30 (.D(WDATA), .en(decoder_1_out29), .Q(register_30_q), .clk(WCLK));  // open: clr
  Register #(.width(16)) register_31 (.D(WDATA), .en(decoder_1_out30), .Q(register_31_q), .clk(WCLK));  // open: clr
  Register #(.width(16)) register_32 (.D(WDATA), .en(decoder_1_out31), .Q(register_32_q), .clk(WCLK));  // open: clr
  Multiplexer #(.select(5), .width(16), .enable("false")) multiplexer_1 (
    .in0(register_1_q), .in1(register_2_q), .in2(register_3_q), .in3(register_4_q), .in4(register_5_q),
    .in5(register_6_q), .in6(register_7_q), .in7(register_8_q), .in8(register_9_q), .in9(register_10_q),
    .in10(register_11_q), .in11(register_12_q), .in12(register_13_q), .in13(register_14_q),
    .in14(register_15_q), .in15(register_16_q), .in16(register_17_q), .in17(register_18_q),
    .in18(register_19_q), .in19(register_20_q), .in20(register_21_q), .in21(register_22_q),
    .in22(register_23_q), .in23(register_24_q), .in24(register_25_q), .in25(register_26_q),
    .in26(register_27_q), .in27(register_28_q), .in28(register_29_q), .in29(register_30_q),
    .in30(register_31_q), .in31(register_32_q), .out(multiplexer_1_out), .sel(RADDR));
  Register #(.width(16)) register_33 (.D(register_34_q), .Q(RDATA), .clk(not_1_out));  // open: en, clr
  Register #(.width(16)) register_34 (.D(multiplexer_1_out), .Q(register_34_q), .clk(RCLK));  // open: en, clr
  not not_1 (not_1_out, RCLK);
endmodule
