// Logisim project square_root.circ as structural Verilog: 1 circuit, main circuit main
module main (
  input  [15:0] Input,
  input  Start_computation,
  output [7:0] result,
  output finished
);

  wire clock_1_out, clock_2_out, clock_3_out, comparator_1_eq, comparator_1_gt, not_2_out, or_1_out;
  wire [7:0] and_1_out, multiplexer_1_out, multiplexer_2_out, multiplexer_3_out, not_1_out, or_2_out,
       register_1_q, register_2_q;
  wire [15:0] bit_extender_1_out, multiplier_1_out;

  Multiplexer #(.width(8), .disabled(0), .enable("false")) multiplexer_1 (
    .in0(8'h80), .in1(multiplexer_3_out), .out(multiplexer_1_out), .sel(Start_computation));
  Clock clock_1 (.out(clock_1_out));
  Register register_1 (.D(multiplexer_1_out), .Q(register_1_q), .clk(clock_1_out));  // open: en, clr
  assign bit_extender_1_out = {{8{1'b0}}, register_1_q};  // Bit_Extender bit_extender_1
  Multiplexer #(.width(8), .disabled(0), .enable("false")) multiplexer_2 (
    .in0(8'h80), .in1({1'b0, register_2_q[7:1]}), .out(multiplexer_2_out), .sel(Start_computation));
  Multiplier #(.width(16)) multiplier_1 (
    .a(bit_extender_1_out), .b(bit_extender_1_out), .out(multiplier_1_out));  // open: cin, cout
  Register register_2 (.D(multiplexer_2_out), .Q(register_2_q), .clk(clock_2_out));  // open: en, clr
  Clock clock_2 (.out(clock_2_out));
  Comparator #(.width(16), .mode("unsigned")) comparator_1 (
    .a(Input), .b(multiplier_1_out), .gt(comparator_1_gt), .eq(comparator_1_eq));  // open: lt
  assign not_1_out = ~register_2_q;  // NOT_Gate not_1, 8 bits wide
  or or_1 (or_1_out, comparator_1_gt, comparator_1_eq);
  assign or_2_out = register_1_q | {1'b0, register_2_q[7:1]};  // OR_Gate or_2, 8 bits wide
  assign and_1_out = not_1_out & or_2_out;  // AND_Gate and_1, 8 bits wide
  Multiplexer #(.width(8), .disabled(0), .enable("false")) multiplexer_3 (
    .in0(and_1_out), .in1(or_2_out), .out(multiplexer_3_out), .sel(or_1_out));
  Comparator #(.mode("unsigned")) comparator_2 (.a({8{1'b0}}), .b(register_2_q), .eq(finished));  // open: gt, lt
  Register register_3 (.D(multiplexer_3_out), .en(not_2_out), .Q(result), .clk(clock_3_out));  // open: clr
  not not_2 (not_2_out, finished);
  Clock clock_3 (.out(clock_3_out));
endmodule
