// Logisim project widthchanger.circ as structural Verilog: 1 circuit, main circuit main
module main (
);

  wire and_1_out, clock_1_out, clock_2_out, clock_3_out, clock_4_out, clock_5_out, comparator_1_lt,
       comparator_2_eq;
  wire [1:0] adder_2_out, multiplexer_2_out, register_5_q;
  wire [3:0] counter_1_q;
  wire [7:0] adder_1_out, multiplexer_1_out, register_1_q, register_2_q;
  wire [31:0] register_4_q, rom_1_data;

  Counter #(.width(4), .max('hf)) counter_1 (.Q(counter_1_q), .clk(clock_1_out));  // open: load, D, count, carry, clr
  Clock clock_1 (.out(clock_1_out));
  Multiplexer #(.width(8), .disabled(0), .enable("false")) multiplexer_1 (
    .in0(register_1_q), .in1(adder_1_out), .out(multiplexer_1_out), .sel(and_1_out));
  Adder adder_1 (.a(register_1_q), .b(8'h1), .out(adder_1_out));  // open: cin, cout
  and and_1 (and_1_out, counter_1_q[0], counter_1_q[1], counter_1_q[2], counter_1_q[3]);
  Clock clock_2 (.out(clock_2_out));
  Register register_1 (.D(multiplexer_1_out), .Q(register_1_q), .clk(clock_3_out));  // open: en, clr
  Clock clock_3 (.out(clock_3_out));
  Register register_2 (.Q(register_2_q), .clk(clock_2_out));  // open: D, en, clr
  Comparator #(.mode("unsigned")) comparator_1 (
    .a(register_2_q), .b(register_1_q), .lt(comparator_1_lt));  // open: gt, eq
  Register #(.width(1)) register_3 (.D(comparator_1_lt), .clk(clock_4_out));  // open: en, Q, clr
  Clock clock_4 (.out(clock_4_out));
  ROM #(.dataWidth(32)) rom_1 (.addr(register_2_q), .data(rom_1_data));  // open: sel
  Register #(.width(32)) register_4 (.D(rom_1_data), .Q(register_4_q), .clk(clock_5_out));  // open: en, clr
  Clock clock_5 (.out(clock_5_out));
  Adder #(.width(2)) adder_2 (.a(register_5_q), .b(2'b01), .out(adder_2_out));  // open: cin, cout
  Multiplexer #(.select(2), .width(2), .disabled(0), .enable("false")) multiplexer_2 (
    .in0(register_5_q), .in1(adder_2_out), .in2(2'b00), .out(multiplexer_2_out));  // open: in3, sel
  Comparator #(.width(2), .mode("unsigned")) comparator_2 (.b(2'b11), .eq(comparator_2_eq));  // open: a, gt, lt
  Register #(.width(2)) register_5 (.D(multiplexer_2_out), .Q(register_5_q));  // open: en, clk, clr
  Multiplexer #(.select(2), .width(8), .disabled(0), .enable("false")) multiplexer_3 (
    .in0(register_4_q[7:0]), .in1(register_4_q[15:8]), .in2(register_4_q[23:16]), .in3(register_4_q[31:24]),
    .sel(register_5_q));  // open: out

  // Notes on the sheet:
  //   contents of rom_1 (hex, n*v repeats v):
  //   11111111 22222222 33333333 44444444 55555555 66666666 77777777 88888888
endmodule
